# Fritzing sketch schematics (saved by Fritzing 0.9.4)
breadboards: 1

parts:
  Part1 = Arduino Nano (Rev3.0)
  Grove1 = Grove OLED 128x96
  HC-SR04_Sensor_1 = HC-SR04 Ultrasonic Distance Sensor
  HC-SR04_Sensor_2 = HC-SR04 Ultrasonic Distance Sensor
  VCC1 = Battery block 9V

nets:
  GND: Part1.GND, Grove1.GND, HC-SR04_Sensor_1.GND, HC-SR04_Sensor_2.GND
  N1: Part1.D2, HC-SR04_Sensor_2.TRIG
  N2: Part1.D3, HC-SR04_Sensor_2.ECHO
  N3: Part1.D11/MOSI, HC-SR04_Sensor_1.ECHO
  N4: Part1.D12/MISO, HC-SR04_Sensor_1.TRIG
  N5: Part1.VIN, VCC1.+
  VCC: Part1.5V, Grove1.VCC, HC-SR04_Sensor_1.VCC, HC-SR04_Sensor_2.VCC, VCC1.-
  N6: Part1.A5, Grove1.SDA
  N7: Part1.A4, Grove1.SCL
